// Digital circuit 1 Bit Buffer.dig as structural Verilog
module _1_Bit_Buffer (
  input  DATA_IN,
  input  WRITE,
  input  ADDR_LINE,
  output DATA_OUT,
  output DATA_OUT_2,
  output DATA_OUT_3,
  output DATA_OUT_4
);

  wire driver_1_out, driver_2_out, driver_3_out, driver_4_out, nfet_1_d, nfet_2_d, nfet_3_d, nfet_4_d;

  assign driver_1_out = WRITE ? DATA_IN : 1'bz;  // Driver driver_1
  assign driver_2_out = WRITE ? DATA_IN : 1'bz;  // Driver driver_2
  assign driver_3_out = WRITE ? DATA_IN : 1'bz;  // Driver driver_3
  assign driver_4_out = WRITE ? DATA_IN : 1'bz;  // Driver driver_4
  NFET nfet_1 (.G(ADDR_LINE), .D(nfet_1_d), .S(driver_1_out));
  NFET nfet_2 (.G(ADDR_LINE), .D(nfet_2_d), .S(driver_2_out));
  NFET nfet_3 (.G(ADDR_LINE), .D(nfet_3_d), .S(driver_3_out));
  NFET nfet_4 (.G(ADDR_LINE), .D(nfet_4_d), .S(driver_4_out));
  Delay delay_1 (.in(nfet_1_d), .out(DATA_OUT));
  Delay delay_2 (.in(nfet_2_d), .out(DATA_OUT_2));
  Delay delay_3 (.in(nfet_3_d), .out(DATA_OUT_3));
  Delay delay_4 (.in(nfet_4_d), .out(DATA_OUT_4));

  // Notes on the sheet:
  //   DATA_IN: DATA IN
  //   WRITE: WRITE
  //   ADDR_LINE: ADDR LINE
  //   DATA_OUT: DATA OUT
  //   DATA_OUT_2: DATA OUT
  //   DATA_OUT_3: DATA OUT
  //   DATA_OUT_4: DATA OUT
endmodule
