// Digital circuit RAM.dig as structural Verilog
module RAM (
  input  ADDR,
  input  DADOS,
  input  in_3
);

  wire nfet_1_d, nfet_3_d, nfet_4_s, not_1_out;

  NFET nfet_1 (.G(ADDR), .D(nfet_1_d), .S(DADOS));
  NFET nfet_2 (.G(nfet_4_s), .D(nfet_1_d), .S(in_3));
  NFET nfet_3 (.G(nfet_4_s), .D(nfet_3_d), .S(nfet_1_d));
  not not_1 (not_1_out, DADOS);
  NFET nfet_4 (.G(nfet_1_d), .D(in_3), .S(nfet_4_s));
  NFET nfet_5 (.G(nfet_1_d), .D(nfet_4_s), .S(nfet_3_d));
  NFET nfet_6 (.G(ADDR), .D(not_1_out), .S(nfet_4_s));

  // Notes on the sheet:
  //   ADDR: ADDR
  //   DADOS: DADOS
endmodule
